// Logisim project logisim.circ as structural Verilog
module main (
  input  in_1,
  input  in_2,
  output out_3,
  output out_4
);

  N_AND n_and_1 (.in_1(in_1), .in_2(in_2), .out_3(out_3));
  X_OR x_or_1 (.in_1(in_1), .in_2(in_2), .out_3(out_4));
endmodule

module N_AND (
  input  in_1,
  input  in_2,
  output out_3
);

  wire and_1_out;

  and and_1 (and_1_out, in_1, in_2);
  not not_1 (out_3, and_1_out);
endmodule

module X_OR (
  input  in_1,
  input  in_2,
  output out_3
);

  wire n_and_1_out_3, or_1_out;

  or or_1 (or_1_out, in_1, in_2);
  N_AND n_and_1 (.in_1(in_1), .in_2(in_2), .out_3(n_and_1_out_3));
  and and_1 (out_3, n_and_1_out_3, or_1_out);
endmodule
